# Fritzing sketch M.aguilera-3°D (saved by Fritzing 0.9.2b)
breadboards: 1

parts:
  Parte1 = Arduino Uno (Rev3)
  U1 = POT [package=pot_mammoth]
  IC1 = L293D [package=THT]
  D1 = Rectifier Diode [part_number=1N4001 package="300 mil [THT]"]
  D2 = Rectifier Diode [part_number=1N4001 package="300 mil [THT]"]
  D3 = Rectifier Diode [part_number=1N4001 package="300 mil [THT]"]
  D4 = Rectifier Diode [part_number=1N4001 package="300 mil [THT]"]
  M1 = DC Motor

nets:
  N1: Parte1.A1, U1.A
  N2: Parte1.D5_PWM, IC1.In_1
  N3: Parte1.D6_PWM, IC1.In_2
  N4: U1.S, IC1.Enable_1, IC1.+Vmotor, IC1.+V, D2.cathode, D3.cathode
  N5: U1.E, IC1.0V, D1.anode, D4.anode
  N6: IC1.Out_1_(_Controlled_by_Enable_1_), D2.anode, D4.cathode, M1.pin_2
  N7: IC1.Out_2_(_Controlled_by_Enable_1_), D1.cathode, D3.anode, M1.pin_1
